# Fritzing sketch filtrasi_air_sketch (saved by Fritzing 0.9.3b)
breadboards: 1

parts:
  M1 = ph-4502c [package=THT]
  U1 = ESP32-38PinWide [part_number=ESP32-38PinWide]
  A1 = TS 300B sensor
  A2 = TS-300B interface
  Part1 = LCD1602-I2C
  A3 = BBAA100043

nets:
  N1: M1.pin3, U1.GPIO33
  N2: M1.pin5, U1.GPIO11, A1.Pin_3, A2.Pin_1, A2.Pin_8, Part1.GND, A3.pin4
  VIN: M1.pin6, U1.VIN, A2.Pin_4, Part1.VCC
  N3: U1.GPIO32, A2.Pin_2
  N4: U1.GPIO5, A3.pin3
  N5: U1.GPIO18, A3.pin2
  N6: U1.GPIO19, A3.pin1
  N7: U1.GPIO21, Part1.SCL
  N8: U1.GPIO22, Part1.SDA
  N9: A1.Pin_1, A2.Pin_5
  N10: A1.Pin_2, A2.Pin_6

custom parts:
  ph-4502c: ph-4502c PH Meter.
  ESP32-38PinWide: Generic 38-Pin ESP32 with wide format (only access to one side of pins on a breadboard) based on Stephen Lilley's HiLetgo ESP-WROOM-32 ESP32 ESP-32S Development Board.
  TS 300B sensor: TS 300B water turbidity sensor.
  TS-300B interface: TS-300B interface.
  LCD1602-I2C: A standard character display, usually with 2x16 characters. Comes in many colors with LCM1602 IIC attached.
  BBAA100043: BBAA100043 traffic light module.
